# Fritzing sketch 实验五 时序逻辑电路（2.2） (saved by Fritzing 0.9.3b)
breadboards: 1

parts:
  IC2 = IC, DIP package, 14 pins [chip_label=74HC04]
  IC4 = IC, DIP package, 14 pins [chip_label=74HC20]
  IC1 = IC, DIP package, 16 pins [chip_label=74LS194]
  IC3 = IC, DIP package, 16 pins [chip_label=74HC151]

nets:
  N1: IC2.pin5, IC4.pin8
  N2: IC2.pin6, IC1.pin10
  N3: IC2.pin7, IC4.pin7, IC1.pin6, IC1.pin8, IC3.pin2, IC3.pin7, IC3.pin8
  N4: IC2.pin10, IC4.pin12
  N5: IC2.pin11, IC1.pin13, IC3.pin9
  N6: IC2.pin12, IC4.pin13
  N7: IC2.pin13, IC1.pin14, IC3.pin10
  N8: IC2.pin14, IC4.pin9, IC4.pin14, IC1.pin9, IC1.pin16, IC3.pin13, IC3.pin15, IC3.pin16
  N9: IC4.pin10, IC1.pin15, IC3.pin11
  N10: IC1.pin1, IC1.pin3, IC1.pin4, IC1.pin5, IC3.pin1, IC3.pin3, IC3.pin4
  N11: IC1.pin2, IC3.pin5
  N12: IC3.pin12, IC3.pin14

notes:
  CP
  Z
