# Fritzing sketch 实验五 时序逻辑电路（2） (saved by Fritzing 0.9.3b)
breadboards: 1

parts:
  IC1 = IC, DIP package, 16 pins [chip_label=74LS161]
  IC2 = IC, DIP package, 16 pins [chip_label=74HC138]
  IC3 = IC, DIP package, 14 pins [chip_label=74HC20]

nets:
  N1: IC1.pin1, IC1.pin7, IC2.pin6
  N2: IC1.pin3, IC1.pin4, IC1.pin5, IC1.pin6, IC1.pin8, IC2.pin4, IC2.pin5, IC2.pin8, IC3.pin7
  N3: IC1.pin9, IC2.pin10, IC3.pin10
  N4: IC1.pin10, IC1.pin16, IC2.pin16, IC3.pin9, IC3.pin14
  N5: IC1.pin12, IC2.pin3
  N6: IC1.pin13, IC2.pin2
  N7: IC1.pin14, IC2.pin1
  N8: IC2.pin13, IC3.pin12
  N9: IC2.pin15, IC3.pin13

notes:
  CP
  Z
